# Fritzing sketch FTDI_Connection (saved by Fritzing 0.9.2b)
breadboards: 1

parts:
  U1 = atmega328 [package=dip]
  S1 = Momentary Switch [package=ksa_sealed_tac_switch]  # not connected
  JACK2 = 2.1mm DC Barrel Jack
  J1 = female pin header, 2 pins [form="♀ (female)"]
  J2 = female pin header, 2 pins [form="♀ (female)"]
  J3 = female pin header, 2 pins [form="♀ (female)"]
  D1 = Rectifier Diode [part_number=1N4001 package="Melf DO-213 AB [SMD]"]
  J4 = female pin header, 2 pins [form="♀ (female)"]
  J5 = female pin header, 2 pins [form="♀ (female)"]
  J6 = female pin header, 2 pins [form="♀ (female)"]

nets:
  N1: U1.VCC, U1.AVCC, U1.AREF
  N2: JACK2.sleeve, D1.anode
  N3: J1.pin1, J1.pin2, J6.pin1, J6.pin2
  N4: J2.pin1, J5.pin1
  N5: J2.pin2, J5.pin2
  N6: J3.pin1, J4.pin1
  N7: J3.pin2, J4.pin2

notes:
  Not all of the Mioduino connections are shown.
  FTDI Cable

custom parts:
  2.1mm DC Barrel Jack: 2.1mm DC Barrel Jack with Thru-Hole Connectors (breadboardable)
