# Fritzing sketch LAB_01 (saved by Fritzing 0.9.2b)
breadboards: 1

parts:
  U1 = atmega328 [package=dip]
  S1 = Momentary Switch [package=ksa_sealed_tac_switch]
  7805 = Voltage Regulator - 5V [package="TO220 [THT]"]
  JACK2 = 2.1mm DC Barrel Jack
  Capacitor1 = Electrolytic Capacitor [capacitance=47µF package="1010 [SMD, electrolytic]"]
  R6 = Resistor [tolerance=±5% resistance=1k package=THT]
  R7 = Resistor [tolerance=±5% resistance=1k package=THT]
  LED4 = LED - 3mm [color="Green (555nm)" package="3 mm [THT]"]
  LED5 = LED - 3mm [color="Red (635nm)" package="3 mm [THT]"]
  XTAL1 = Crystal [frequency="16 Mhz" package=THT]
  R8 = Resistor [tolerance=±5% resistance=10k package="0603 [SMD]"]
  C2 = Ceramic Capacitor [capacitance=0.1µF package="0603 [SMD, multilayer]"]
  C3 = Ceramic Capacitor [capacitance=20pF package="100 mil [THT, multilayer]"]
  J1 = female pin header, 2 pins [form="♀ (female)"]
  J2 = female pin header, 2 pins [form="♀ (female)"]
  J3 = female pin header, 2 pins [form="♀ (female)"]
  C4 = Ceramic Capacitor [capacitance=0.1µF package="0603 [SMD, multilayer]"]
  C5 = Ceramic Capacitor [capacitance=0.1µF package="0603 [SMD, multilayer]"]
  Capacitor2 = Electrolytic Capacitor [capacitance=10µF package="1010 [SMD, electrolytic]"]
  D1 = Rectifier Diode [part_number=1N4001 package="Melf DO-213 AB [SMD]"]
  C6 = Ceramic Capacitor [capacitance=20pF package="100 mil [THT, multilayer]"]

nets:
  N1: U1.RESET, S1.3, R8.Pin_1, C2.1
  N2: U1.D0_(RX), J2.pin2
  N3: U1.D1_(TX), J3.pin1
  N4: U1.VCC, U1.AVCC, U1.AREF, R6.Pin_0, R8.Pin_0, J2.pin1, C4.0, C5.1, Capacitor2.+
  N5: U1.GND, LED4.cathode, LED5.anode, C3.1, J1.pin1, J1.pin2, C4.1, C5.0, Capacitor2.-, C6.1
  N6: U1.XLAT1, XTAL1.pin_1, C3.0
  N7: U1.XLAT2, XTAL1.pin_0, C6.0
  N8: U1.D13, R7.Pin_1
  N9: 7805.input_voltage, Capacitor1.+, D1.cathode
  N10: 7805.GND, Capacitor1.-
  N11: JACK2.sleeve, D1.anode
  N12: R6.Pin_1, LED5.cathode
  N13: R7.Pin_0, LED4.anode
  N14: C2.0, J3.pin2

custom parts:
  2.1mm DC Barrel Jack: 2.1mm DC Barrel Jack with Thru-Hole Connectors (breadboardable)
