# Fritzing sketch LAB_03 (saved by Fritzing 0.9.2b)
breadboards: 1

parts:
  U1 = atmega328 [package=dip]
  R1 = Resistor [tolerance=±5% resistance=100 package=THT]
  LED1 = LED - 3mm [color="Blue (430nm)" package="3 mm [THT]"]

nets:
  N1: U1.D3_(PWM), R1.Pin_0
  N2: U1.VCC, U1.AVCC, U1.AREF, LED1.anode
  N3: R1.Pin_1, LED1.cathode

notes:
  Note the orientation of the chip. The dot represents the RST pin. Not all of the Mioduino connections are shown.
