# Fritzing sketch LAB_05 (saved by Fritzing 0.9.2b)
breadboards: 1

parts:
  U1 = atmega328 [package=dip]
  R1 = Resistor [tolerance=±5% resistance=100 package=THT]
  LED1 = LED - 3mm [color="Blue (430nm)" package="3 mm [THT]"]
  S1 = Momentary Switch [package=ksa_sealed_tac_switch]
  R2 = Resistor [tolerance=±5% resistance=100k package=THT]

nets:
  N1: U1.D2, S1.1, R2.Pin_1
  N2: U1.D3_(PWM), R1.Pin_0
  N3: U1.VCC, U1.AVCC, U1.AREF, LED1.anode, R2.Pin_0
  N4: U1.GND, S1.3
  N5: R1.Pin_1, LED1.cathode

notes:
  Note the orientation of the chip. The dot represents the RST pin. Not all of the Mioduino connections are shown.
