# Fritzing sketch LAB_07 (saved by Fritzing 0.9.2b)
breadboards: 1

parts:
  U1 = atmega328 [package=dip]
  R1 = Resistor [tolerance=±5% resistance=10k package=THT]
  POT2 = Breadboard Trimpot

nets:
  N1: U1.VCC, POT2.PIN2
  N2: U1.GND#7, R1.Pin_0
  N3: U1.AVCC, U1.AREF
  N4: U1.A0, R1.Pin_1, POT2.PIN3

notes:
  Note the orientation of the chip. The dot represents the RST pin. Not all of the Mioduino connections are shown.
