# Fritzing sketch LAB_08 (saved by Fritzing 0.9.2b)
breadboards: 1

parts:
  U1 = atmega328 [package=dip]
  U2 = TMP36 [package=to-92-kit]

nets:
  VCC: U1.VCC, U2.VCC
  N1: U1.GND#7, U2.GND
  N2: U1.AVCC, U1.AREF
  N3: U1.A0, U2.VOUT

notes:
  Note the orientation of the chip. The dot represents the RST pin. Not all of the Mioduino connections are shown.
