# Fritzing sketch LAB_09 (saved by Fritzing 0.9.2b)
breadboards: 1

parts:
  U1 = atmega328 [package=dip]
  Q1 = PHOTOTRANSISTOR REFLECTIVE OBJECT SENSOR [package=qrb1114-side]
  R1 = Resistor [tolerance=±5% resistance=470 package="2010 [SMD]"]
  R2 = Resistor [tolerance=±5% resistance=10k package="2010 [SMD]"]

nets (from the breadboard view):
  N1: U1.D9_(PWM), Q1.C, R2.Pin_0
  N2: U1.D12, R1.Pin_0
  N3: U1.AVCC, U1.AREF, R2.Pin_1
  N4: U1.GND#21, Q1.E, Q1.K
  N5: Q1.A, R1.Pin_1

notes:
  Note the orientation of the chip. The dot represents the RST pin. Not all of the Mioduino connections are shown.
