# Fritzing sketch LAB_10 (saved by Fritzing 0.9.2b)
breadboards: 1

parts:
  U1 = atmega328 [package=dip]
  U2 = IC, SIP package, 8 pins [chip_label=MCP9808]

nets:
  N1: U1.VCC, U2.pin1
  N2: U1.GND#7, U2.pin2
  N3: U1.AVCC, U1.AREF
  N4: U1.A4, U2.pin4
  N5: U1.A5, U2.pin3

notes:
  Note the orientation of the chip. The dot represents the RST pin. Not all of the Mioduino connections are shown.
