# Fritzing sketch LAB_11 (saved by Fritzing 0.9.3b)
breadboards: 1

parts:
  U1 = atmega328 [package=dip]
  N1 = Adafruit Breadboard-Friendly NeoPixel [part_number="Adafruit #1312"]
  N2 = Adafruit Breadboard-Friendly NeoPixel [part_number="Adafruit #1312"]
  R1 = Resistor [tolerance=±5% resistance=220 package="0603 [SMD]"]

nets:
  N1: U1.D3_(PWM), R1.Pin_0
  VDD: U1.VCC, N1.VDD, N2.VDD
  GND: U1.GND#7, N1.GND, N2.GND
  N2: U1.AVCC, U1.AREF
  N3: N1.IN, R1.Pin_1
  N4: N1.OUT, N2.IN

notes:
  Note the orientation of the chip. The dot represents the RST pin. Not all of the Mioduino connections are shown.

custom parts:
  Adafruit Breadboard-Friendly NeoPixel: This is the easiest way possible to add small, bright RGB pixels to your project. We took the same technology from our Flora NeoPixels and made them breadboard friendly, with two rows of 3 x 0.1" spaced header on each side for easy soldering, chaining and breadboarding. These ultra-bright LEDs have a constant-current driver cooked right into the LED package! The pixels are chainable - so you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
