# Fritzing sketch Mioduino (saved by Fritzing 0.9.3b)
circuit board: 10cm x 7.62cm

parts:
  ATmega328P = atmega328 [package=dip]
  7805 = Voltage Regulator - 5V [package="TO220 [THT]"]
  R1 = Resistor [tolerance=±5% resistance=1k package=THT]
  R2 = Resistor [tolerance=±5% resistance=1k package=THT]
  D13 = LED - 3mm [color="Green (555nm)" package="3 mm [THT]"]
  POWER = LED - 3mm [color="Red (635nm)" package="3 mm [THT]"]
  Crystal = Crystal [frequency="16 Mhz" package=THT]
  C7 = Ceramic Capacitor [capacitance=20pF package="100 mil [THT, multilayer]"]
  C6 = Ceramic Capacitor [capacitance=20pF package="100 mil [THT, multilayer]"]
  R3 = Resistor [tolerance=±5% resistance=10k package=THT]
  C1 = Ceramic Capacitor [capacitance=0.1µF package="100 mil [THT, multilayer]"]
  C2 = Electrolytic Capacitor [capacitance=47µF package="100 mil [THT, electrolytic]"]
  C3 = Ceramic Capacitor [capacitance=0.1µF package="100 mil [THT, multilayer]"]
  C4 = Ceramic Capacitor [capacitance=0.1µF package="100 mil [THT, multilayer]"]
  C5 = Electrolytic Capacitor [capacitance=100µF package="100 mil [THT, electrolytic]"]
  D2 = Rectifier Diode [part_number=1N4001 package="300 mil [THT]"]
  C8 = Ceramic Capacitor [capacitance=0.1µF package="100 mil [THT, multilayer]"]
  D1 = Rectifier Diode [part_number=1N4001 package="300 mil [THT]"]
  FTDI = female pin header, 6 pins [form="♀ (female)"]
  Analog = female pin header, 6 pins [form="♀ (female)"]
  5V = female pin header, 8 pins [form="♀ (female)"]
  GND = female pin header, 8 pins [form="♀ (female)"]
  DC_POWER = 2.1mm DC Barrel Jack
  Vin = female pin header, 2 pins [form="♀ (female)"]
  Digital = female pin header, 14 pins [form="♀ (female)"]
  Reset = SWITCH-MOMENTARY-2 [package=tactile-pth-12mm]

nets:
  N1: ATmega328P.RESET, R3.Pin_1, C8.1, Reset.1
  D0: ATmega328P.D0_(RX), FTDI.pin4, Digital.pin14
  D1: ATmega328P.D1_(TX), FTDI.pin5, Digital.pin13
  D2: ATmega328P.D2, Digital.pin12
  D3: ATmega328P.D3_(PWM), Digital.pin11
  D4: ATmega328P.D4, Digital.pin10
  5V: ATmega328P.VCC, ATmega328P.AVCC, ATmega328P.AREF, 7805.output_voltage, R1.Pin_1, R3.Pin_0, C3.1, C4.1, C5.+, D2.cathode, 5V.pin1, 5V.pin2, 5V.pin3, 5V.pin4, 5V.pin5, 5V.pin6, 5V.pin7, 5V.pin8
  GND: ATmega328P.GND, 7805.GND, D13.cathode, POWER.cathode, C7.1, C6.1, C1.0, C2.-, C3.0, C4.0, C5.-, FTDI.pin1, FTDI.pin2, GND.pin1, GND.pin2, GND.pin3, GND.pin4, GND.pin5, GND.pin6, GND.pin7, GND.pin8, DC_POWER.switch, DC_POWER.sleeve, Vin.pin1, Reset.2
  N2: ATmega328P.XLAT1, Crystal.pin_0, C6.0
  N3: ATmega328P.XLAT2, Crystal.pin_1, C7.0
  N4: ATmega328P.D5_(PWM), Digital.pin9
  N5: ATmega328P.D6_(PWM), Digital.pin8
  N6: ATmega328P.D7, Digital.pin7
  N7: ATmega328P.D8, Digital.pin6
  N8: ATmega328P.D9_(PWM), Digital.pin5
  N9: ATmega328P.D10_(PWM), Digital.pin4
  N10: ATmega328P.D11_(PWM), Digital.pin3
  N11: ATmega328P.D12, Digital.pin2
  N12: ATmega328P.D13, R2.Pin_0, Digital.pin1
  N13: ATmega328P.A0, Analog.pin1
  N14: ATmega328P.A1, Analog.pin2
  N15: ATmega328P.A2, Analog.pin3
  N16: ATmega328P.A3, Analog.pin4
  N17: ATmega328P.A4, Analog.pin5
  N18: ATmega328P.A5, Analog.pin6
  N19: 7805.input_voltage, C1.1, C2.+, D1.cathode
  N20: R1.Pin_0, POWER.anode
  N21: R2.Pin_1, D13.anode
  N22: D2.anode, FTDI.pin3
  N23: C8.0, FTDI.pin6
  Vin: D1.anode, DC_POWER.center, Vin.pin2

notes:
  Mioduino, Schematic diagram for the Mioduino by Daniel Porrey, 1.05
  5V Power Supply
  Reset
  FTDI Interface
  Clock
  Power LED
  Activity LED
  Input: 7-35V
  1
  D2
  D3
  D4
  D5
  D6
  D7
  D8
  D9
  D10
  D11
  D12
  A0
  A1
  A2
  A3
  A4
  A5
  Mioduino Prototype Board
  designed by Daniel M. Porrey
  v1.0.6 - December 2018
  GND
  125Ω to 1KΩ
  135Ω to 1KΩ
  10K
  20pF
  0.1µF
  47µF
  100µF
  16 MHz
  D0
  D1
  Power Rail
  Ground Rail
  +
  -
  15
  Red
  Green
  (Green)
  (Red)
  VIN
  IN
  OUT
  5V
  TXD
  CTS
  RXD
  RTS
  1.9V - 2.3V FV @ 20mA
  2.0V - 2.5V FV @ 20mA
  with bootloader
  VIN Header
  Digital Header
  Analog Header
  DC Power Jack
  D13

custom parts:
  2.1mm DC Barrel Jack: 2.1mm DC Barrel Jack with Thru-Hole Connectors (breadboardable)
